// Logisim project Clock.circ as structural Verilog: 9 circuits, main circuit clockCompleto
module clockCompleto (
);

  wire clock2_1_vai1, clock5_1_vai1, clock5_2_vai1, clock9_1_vai1, clock9_2_vai1, clock9_3_vai1, clock_1_out;
  wire [3:0] clock2_1_s, clock4_1_s, clock5_1_s, clock5_2_s, clock9_1_s, clock9_2_s, clock9_3_s,
       multiplexer_1_out;

  Clock clock_1 (.out(clock_1_out));
  clock2 clock2_1 (.CLK(clock9_1_vai1), .S(clock2_1_s), .Vai1(clock2_1_vai1));
  clock4 clock4_1 (.CLK(clock9_1_vai1), .S(clock4_1_s));  // open: Vai1
  Hex_Digit_Display hex_digit_display_1 (.value(clock2_1_s), .dp(1'b0));
  clock9 clock9_1 (.CLK(clock5_1_vai1), .S(clock9_1_s), .Vai1(clock9_1_vai1));
  Multiplexer #(.width(4), .enable("false")) multiplexer_1 (
    .in0(clock4_1_s), .in1(clock9_1_s), .out(multiplexer_1_out), .sel(clock2_1_vai1));
  Hex_Digit_Display hex_digit_display_2 (.value(multiplexer_1_out), .dp(1'b0));
  Hex_Digit_Display hex_digit_display_3 (.value(clock5_1_s), .dp(1'b0));
  clock5 clock5_1 (.CLK(clock9_2_vai1), .S(clock5_1_s), .Vai1(clock5_1_vai1));
  Hex_Digit_Display hex_digit_display_4 (.value(clock9_2_s), .dp(1'b0));
  clock9 clock9_2 (.CLK(clock5_2_vai1), .S(clock9_2_s), .Vai1(clock9_2_vai1));
  Hex_Digit_Display hex_digit_display_5 (.value(clock9_3_s), .dp(1'b0));
  Hex_Digit_Display hex_digit_display_6 (.value(clock5_2_s), .dp(1'b0));
  clock9 clock9_3 (.CLK(clock_1_out), .S(clock9_3_s), .Vai1(clock9_3_vai1));
  clock5 clock5_2 (.CLK(clock9_3_vai1), .S(clock5_2_s), .Vai1(clock5_2_vai1));
endmodule

module proxEstado9 (
  input  a,
  input  b,
  input  c,
  input  d,
  output sa,
  output sb,
  output sc,
  output sd
);

  wire and_1_out, and_2_out, and_3_out, and_4_out, and_5_out, and_6_out, and_7_out, not_1_out, not_2_out,
       not_3_out, not_4_out, not_5_out, not_6_out, not_7_out;

  and and_1 (and_1_out, b, c, d);
  and and_2 (and_2_out, a, not_1_out);
  not not_1 (not_1_out, d);
  not not_2 (not_2_out, b);
  and and_3 (and_3_out, not_2_out, c, d);
  and and_4 (and_4_out, b, not_3_out);
  not not_3 (not_3_out, c);
  and and_5 (and_5_out, b, not_4_out);
  not not_4 (not_4_out, d);
  not not_5 (not_5_out, a);
  and and_6 (and_6_out, not_5_out, not_6_out, d);
  not not_6 (not_6_out, c);
  and and_7 (and_7_out, c, not_7_out);
  not not_7 (not_7_out, d);
  not not_8 (sd, d);
  or or_1 (sa, and_1_out, and_2_out);
  or or_2 (sb, and_3_out, and_4_out, and_5_out);
  or or_3 (sc, and_6_out, and_7_out);
endmodule

module proxEstado5 (
  input  a,
  input  b,
  input  c,
  output sa,
  output sb,
  output sc
);

  wire and_1_out, and_2_out, and_3_out, and_4_out, not_1_out, not_2_out, not_3_out, not_4_out;

  not not_1 (not_1_out, c);
  not not_2 (not_2_out, a);
  not not_3 (not_3_out, b);
  not not_4 (not_4_out, c);
  not not_5 (sc, c);
  and and_1 (and_1_out, b, c);
  and and_2 (and_2_out, a, not_1_out);
  and and_3 (and_3_out, not_2_out, not_3_out, c);
  and and_4 (and_4_out, b, not_4_out);
  or or_1 (sa, and_1_out, and_2_out);
  or or_2 (sb, and_3_out, and_4_out);
endmodule

// CLK5
module clock5 (
  input  CLK,
  output [3:0] S,
  output Vai1
);

  wire proxestado5_1_sa, proxestado5_1_sb, proxestado5_1_sc;

  D_Flip_Flop d_ff_1 (.clk(CLK), .D(proxestado5_1_sa), .Q(S[2]));  // open: Qn, preset, en, reset
  proxEstado5 proxestado5_1 (
    .a(S[2]), .b(S[1]), .c(S[0]), .sa(proxestado5_1_sa), .sb(proxestado5_1_sb), .sc(proxestado5_1_sc));
  D_Flip_Flop d_ff_2 (.clk(CLK), .D(proxestado5_1_sb), .Q(S[1]));  // open: Qn, preset, en, reset
  D_Flip_Flop d_ff_3 (.clk(CLK), .D(proxestado5_1_sc), .Q(S[0]));  // open: Qn, preset, en, reset
  and and_1 (Vai1, ~S[0], ~S[1], ~S[2]);  // AND_Gate

  assign S[3] = 1'b0;
endmodule

// CLK9
module clock9 (
  input  CLK,
  output [3:0] S,
  output Vai1
);

  wire proxestado9_1_sa, proxestado9_1_sb, proxestado9_1_sc, proxestado9_1_sd;

  D_Flip_Flop d_ff_1 (.clk(CLK), .D(proxestado9_1_sa), .Q(S[3]));  // open: Qn, preset, en, reset
  proxEstado9 proxestado9_1 (
    .a(S[3]), .b(S[2]), .c(S[1]), .d(S[0]), .sa(proxestado9_1_sa), .sb(proxestado9_1_sb),
    .sc(proxestado9_1_sc), .sd(proxestado9_1_sd));
  D_Flip_Flop d_ff_2 (.clk(CLK), .D(proxestado9_1_sb), .Q(S[2]));  // open: Qn, preset, en, reset
  D_Flip_Flop d_ff_3 (.clk(CLK), .D(proxestado9_1_sc), .Q(S[1]));  // open: Qn, preset, en, reset
  D_Flip_Flop d_ff_4 (.clk(CLK), .D(proxestado9_1_sd), .Q(S[0]));  // open: Qn, preset, en, reset
  and and_1 (Vai1, ~S[0], ~S[1], ~S[2], ~S[3]);  // AND_Gate
endmodule

module proxEstado4 (
  input  a,
  input  b,
  input  c,
  output sa,
  output sb,
  output sc
);

  wire and_2_out, and_3_out, not_1_out, not_2_out, not_3_out, not_4_out;

  and and_1 (sa, b, c);
  not not_1 (not_1_out, b);
  not not_2 (not_2_out, c);
  not not_3 (not_3_out, a);
  not not_4 (not_4_out, c);
  and and_2 (and_2_out, not_1_out, c);
  and and_3 (and_3_out, b, not_2_out);
  and and_4 (sc, not_3_out, not_4_out);
  or or_1 (sb, and_2_out, and_3_out);
endmodule

module proxEstado2 (
  input  a,
  input  b,
  output sa,
  output sb
);

  wire not_1_out, not_2_out;

  not not_1 (not_1_out, a);
  not not_2 (not_2_out, b);
  and and_1 (sb, not_1_out, not_2_out);

  assign sa = b;
endmodule

// CLK4
module clock4 (
  input  CLK,
  output [3:0] S,
  output Vai1
);

  wire proxestado4_1_sa, proxestado4_1_sb, proxestado4_1_sc;

  D_Flip_Flop d_ff_1 (.clk(CLK), .D(proxestado4_1_sa), .Q(S[2]));  // open: Qn, preset, en, reset
  proxEstado4 proxestado4_1 (
    .a(S[2]), .b(S[1]), .c(S[0]), .sa(proxestado4_1_sa), .sb(proxestado4_1_sb), .sc(proxestado4_1_sc));
  D_Flip_Flop d_ff_2 (.clk(CLK), .D(proxestado4_1_sb), .Q(S[1]));  // open: Qn, preset, en, reset
  D_Flip_Flop d_ff_3 (.clk(CLK), .D(proxestado4_1_sc), .Q(S[0]));  // open: Qn, preset, en, reset
  and and_1 (Vai1, ~S[0], ~S[1], ~S[2]);  // AND_Gate

  assign S[3] = 1'b0;
endmodule

// CLK2
module clock2 (
  input  CLK,
  output [3:0] S,
  output Vai1
);

  wire proxestado2_1_sa, proxestado2_1_sb;

  proxEstado2 proxestado2_1 (.a(S[1]), .b(S[0]), .sa(proxestado2_1_sa), .sb(proxestado2_1_sb));
  D_Flip_Flop d_ff_1 (.clk(CLK), .D(proxestado2_1_sa), .Q(S[1]));  // open: Qn, preset, en, reset
  D_Flip_Flop d_ff_2 (.clk(CLK), .D(proxestado2_1_sb), .Q(S[0]));  // open: Qn, preset, en, reset
  and and_1 (Vai1, ~S[0], ~S[1]);  // AND_Gate

  assign S[3:2] = 2'b00;
endmodule
